# Fritzing sketch flex_led (saved by Fritzing 0.8.0b)
breadboards: 1

parts:
  Composants1 = Arduino Uno (Rev3)
  R1 = Resistor [tolerance=±5% resistance=22k package=THT]
  R3 = Resistor [tolerance=±5% resistance=330 package=THT]
  LED1 = LED - 5mm [color="Red (633nm)" package="5 mm [THT]"]
  R2 = Basic Flex Resistor

nets:
  N1: Composants1.A0, R1.Pin_0, R2.pin_1
  N2: Composants1.GND, LED1.cathode
  N3: Composants1.D3_PWM, R3.Pin_0
  N4: Composants1.5V, R2.Pin_2
  N5: R3.Pin_1, LED1.anode
